// Logisim project cpu.circ as structural Verilog: 11 circuits, main circuit main
module main (
  input  [31:0] INSTRUCTION,
  input  CLOCK,
  output [31:0] FETCH_ADDRESS,
  output [31:0] ra_Value,
  output [31:0] sp_Value,
  output [31:0] t0_Value,
  output [31:0] t1_Value,
  output [31:0] t2_Value,
  output [31:0] s0_Value,
  output [31:0] s1_Value,
  output [31:0] a0_Value
);

  wire and_1_out, ASel, BLT, BrEq, BrUn, BSel, MEM_p1, MEM_p3, MEM_p8, MEM_p12, MEM_p14, MemRW, PCSel, RegWEn;
  wire [1:0] WBSel;
  wire [2:0] FUNCT3;
  wire [3:0] ALUSel, ImmSel;
  wire [6:0] OPCODE;
  wire [31:0] ALU, Imm, MEM, MEM_p10, MEM_p15, multiplexer_1_out, multiplexer_2_out, multiplexer_3_out,
       multiplexer_4_out, multiplier_1_out, PC__4, RS1, RS2, WB;

  Register #(.width(32)) PC (.D(multiplexer_1_out), .Q(FETCH_ADDRESS), .clk(CLOCK));  // open: en, clr
  Multiplexer #(.width(32)) multiplexer_1 (.in0(ALU), .in1(PC__4), .out(multiplexer_1_out), .sel(PCSel));  // open: en
  // Probe on FETCH_ADDRESS
  Adder #(.width(32)) adder_1 (.a(FETCH_ADDRESS), .b(32'h1), .out(PC__4));  // open: cin, cout
  Multiplexer #(.width(32)) multiplexer_2 (
    .in0(WB), .in1(multiplier_1_out), .out(multiplexer_2_out), .sel(and_1_out));  // open: en
  Multiplier #(.width(32)) multiplier_1 (.a(WB), .b(32'h4), .out(multiplier_1_out));  // open: cin, cout
  and and_1 (and_1_out, ASel, BSel);
  regfile_main main_1 (
    .Read_Register_1__rs1(INSTRUCTION[19:15]), .Read_Register_2__rs2(INSTRUCTION[24:20]),
    .Write_Register__rd(INSTRUCTION[11:7]), .Write_Data(multiplexer_2_out), .Write_Enable(RegWEn),
    .Clock(CLOCK), .Read_Data_1(RS1), .Read_Data_2(RS2), .ra_Value(ra_Value), .sp_Value(sp_Value),
    .t0_Value(t0_Value), .t1_Value(t1_Value), .t2_Value(t2_Value), .s0_Value(s0_Value), .s1_Value(s1_Value),
    .a0_Value(a0_Value));
  ImmGenerator immgenerator_1 (.Instruction(INSTRUCTION), .ImmSel(ImmSel), .Immediate(Imm));
  Control control_1 (
    .Instruction(INSTRUCTION), .PCSel(PCSel), .ImmSel(ImmSel), .RegWEn(RegWEn), .BrUn(BrUn), .ASel(ASel),
    .BSel(BSel), .ALUSel(ALUSel), .MemRW(MemRW), .WBSel(WBSel), .BrEq(BrEq), .BLT(BLT), .OPCODE(OPCODE),
    .FUNCT3(FUNCT3));
  Multiplexer #(.width(32)) multiplexer_3 (
    .in0(RS1), .in1(FETCH_ADDRESS), .out(multiplexer_3_out), .sel(ASel));  // open: en
  Multiplexer #(.width(32)) multiplexer_4 (.in0(RS2), .in1(Imm), .out(multiplexer_4_out), .sel(BSel));  // open: en
  alu_main main_2 (.Switch(ALUSel), .X(multiplexer_3_out), .Result(ALU), .Y(multiplexer_4_out));  // open: Equal
  Branch_Comparator branch_comparator_1 (.in_1(RS1), .in_2(RS2), .BrEq(BrEq), .in_3(BrUn), .BLT(BLT));
  // mem_main MEM: pin names not known; wires that end beside it: MEM_p1, MEM_p1, MEM_p3, MEM_p3, ALU, RS2, MemRW, MEM_p8, CLOCK, MEM_p10, MEM_p8, MEM_p12, MEM_p12, MEM_p14, MEM_p15
  SignExt signext_1 (.MEM(MEM_p10), .OP(OPCODE), .F3(FUNCT3), .OUT(MEM));
  Multiplexer #(.select(2), .width(32)) multiplexer_5 (
    .in0(MEM), .in1(MEM_p15), .in2(PC__4), .in3(ALU), .out(WB), .sel(WBSel));  // open: en

  // Other names for the same wires on the sheet: a0[31:0] = a0_Value; clk = CLOCK; fetch_addr[31:0] = FETCH_ADDRESS;
  //   PC[31:0] = FETCH_ADDRESS; ra[31:0] = ra_Value; s0[31:0] = s0_Value; s1[31:0] = s1_Value; sp[31:0] = sp_Value;
  //   t0[31:0] = t0_Value; t1[31:0] = t1_Value; t2[31:0] = t2_Value

  // Notes on the sheet:
  //   Output
  //   These are outputs/inputs from run.circ
  //   Inputs
endmodule

module Control (
  input  [31:0] Instruction,
  input  BrEq,
  input  BLT,
  output PCSel,
  output [3:0] ImmSel,
  output RegWEn,
  output BrUn,
  output ASel,
  output BSel,
  output [3:0] ALUSel,
  output MemRW,
  output [1:0] WBSel,
  output [6:0] OPCODE,
  output [2:0] FUNCT3
);

  wire and_1_out, comparator_1_eq, comparator_2_eq, comparator_3_eq, comparator_4_eq, jump_1_select_alu;
  wire [3:0] op;

  // Probe on Instruction[6:0]
  // Probe on op
  opcode_ID opcode_id_1 (.in_1(Instruction[6:0]), .out_2(op));
  Jump jump_1 (
    .BrEq(BrEq), .BLT(BLT), .opcode(Instruction[6:0]), .funct3(Instruction[14:12]),
    .Select_ALU(jump_1_select_alu));
  Comparator #(.width(7)) comparator_1 (.a(Instruction[6:0]), .b(7'b1100011), .eq(comparator_1_eq));  // open: gt, lt
  Comparator #(.width(3)) comparator_2 (.a(Instruction[14:12]), .b(3'b110), .eq(comparator_2_eq));  // open: gt, lt
  Multiplexer multiplexer_1 (.in0(1'b1), .in1(1'b0), .out(PCSel), .sel(jump_1_select_alu));  // open: en
  Multiplexer multiplexer_2 (.in0(1'b1), .in1(1'b0), .out(RegWEn), .sel(comparator_3_eq));  // open: en
  Comparator #(.width(2)) comparator_3 (.a(2'b10), .b(op[2:1]), .eq(comparator_3_eq));  // open: gt, lt
  Multiplexer multiplexer_3 (.in0(1'b0), .in1(1'b1), .out(MemRW), .sel(comparator_4_eq));  // open: en
  Comparator #(.width(4)) comparator_4 (.a(4'b0100), .b(op), .eq(comparator_4_eq));  // open: gt, lt
  ALUSel alusel_1 (.OP(Instruction[6:0]), .FUNCT3(Instruction[14:12]), .FUNCT7(Instruction[31:25]), .out_4(ALUSel));
  ImmSel immsel_1 (.opcode(Instruction[6:0]), .ImmSel(ImmSel));
  ABSel absel_1 (.opcode(Instruction[6:0]), .funct3(Instruction[14:12]), .ASel(ASel), .BSel(BSel));
  Multiplexer multiplexer_4 (.in0(1'b0), .in1(1'b1), .out(BrUn), .sel(and_1_out));  // open: en
  and and_1 (and_1_out, comparator_1_eq, comparator_2_eq);
  WBSel wbsel_1 (.OP(Instruction[6:0]), .FUNCT3(Instruction[14:12]), .FUNCT7(Instruction[31:25]), .WBSel(WBSel));

  assign FUNCT3 = Instruction[14:12];
  assign OPCODE = Instruction[6:0];

  // Other names for the same wires on the sheet: funct7[6:0] = Instruction[31:25]
endmodule

module opcode_ID (
  input  [6:0] in_1,
  output [3:0] out_2
);

  wire comparator_1_eq, comparator_2_eq, comparator_3_eq, comparator_4_eq, comparator_5_eq, comparator_6_eq,
       comparator_7_eq, comparator_8_eq;
  wire [3:0] multiplexer_1_out, multiplexer_2_out, multiplexer_3_out, multiplexer_4_out, multiplexer_5_out,
       multiplexer_6_out, multiplexer_7_out, multiplexer_8_out;

  Comparator #(.width(7)) comparator_1 (.a(7'b0110011), .b(in_1), .eq(comparator_1_eq));  // open: gt, lt
  Comparator #(.width(7)) comparator_2 (.a(7'b0000011), .b(in_1), .eq(comparator_2_eq));  // open: gt, lt
  Comparator #(.width(7)) comparator_3 (.a(7'b0010011), .b(in_1), .eq(comparator_3_eq));  // open: gt, lt
  Comparator #(.width(7)) comparator_4 (.a(7'b0100011), .b(in_1), .eq(comparator_4_eq));  // open: gt, lt
  Comparator #(.width(7)) comparator_5 (.a(7'b1100011), .b(in_1), .eq(comparator_5_eq));  // open: gt, lt
  Comparator #(.width(7)) comparator_6 (.a(7'b0110111), .b(in_1), .eq(comparator_6_eq));  // open: gt, lt
  Comparator #(.width(7)) comparator_7 (.a(7'b1101111), .b(in_1), .eq(comparator_7_eq));  // open: gt, lt
  Comparator #(.width(7)) comparator_8 (.a(7'b1100111), .b(in_1), .eq(comparator_8_eq));  // open: gt, lt
  Multiplexer #(.width(4)) multiplexer_1 (
    .in0(4'b0000), .in1(4'b0001), .out(multiplexer_1_out), .sel(comparator_1_eq));  // open: en
  Multiplexer #(.width(4)) multiplexer_2 (
    .in0(4'b0000), .in1(4'b0010), .out(multiplexer_2_out), .sel(comparator_2_eq));  // open: en
  Multiplexer #(.width(4)) multiplexer_3 (
    .in0(4'b0000), .in1(4'b0011), .out(multiplexer_3_out), .sel(comparator_3_eq));  // open: en
  Multiplexer #(.width(4)) multiplexer_4 (
    .in0(4'b0000), .in1(4'b0100), .out(multiplexer_4_out), .sel(comparator_4_eq));  // open: en
  Multiplexer #(.width(4)) multiplexer_5 (
    .in0(4'b0000), .in1(4'b0101), .out(multiplexer_5_out), .sel(comparator_5_eq));  // open: en
  Multiplexer #(.width(4)) multiplexer_6 (
    .in0(4'b0000), .in1(4'b0110), .out(multiplexer_6_out), .sel(comparator_6_eq));  // open: en
  Multiplexer #(.width(4)) multiplexer_7 (
    .in0(4'b0000), .in1(4'b0111), .out(multiplexer_7_out), .sel(comparator_7_eq));  // open: en
  Multiplexer #(.width(4)) multiplexer_8 (
    .in0(4'b0000), .in1(4'b1000), .out(multiplexer_8_out), .sel(comparator_8_eq));  // open: en
  assign out_2 = multiplexer_1_out | multiplexer_2_out | multiplexer_3_out | multiplexer_4_out | multiplexer_5_out | multiplexer_6_out | multiplexer_7_out | multiplexer_8_out;  // OR_Gate or_1, 4 bits wide

  // Other names for the same wires on the sheet: opcode[6:0] = in_1

  // Notes on the sheet:
  //   R-type
  //   LOAD
  //   I-type
  //   S-type
  //   SB-type
  //   LUI
  //   JAL
  //   JALR
endmodule

module Jump (
  input  [6:0] opcode,
  input  [2:0] funct3,
  input  BrEq,
  input  BLT,
  output Select_ALU
);

  wire and_1_out, and_2_out, comparator_1_eq, comparator_2_eq, comparator_3_eq, comparator_4_eq,
       comparator_5_eq, comparator_6_eq, comparator_7_eq, or_1_out, or_2_out;

  Comparator #(.width(7)) comparator_1 (.a(7'b1101111), .b(opcode), .eq(comparator_1_eq));  // open: gt, lt
  Comparator #(.width(7)) comparator_2 (.a(opcode), .b(7'b1100111), .eq(comparator_2_eq));  // open: gt, lt
  Comparator #(.width(7)) comparator_3 (.a(opcode), .b(7'b1100011), .eq(comparator_3_eq));  // open: gt, lt
  Comparator #(.width(3)) comparator_4 (.a(funct3), .b(3'b000), .eq(comparator_4_eq));  // open: gt, lt
  Comparator #(.width(7)) comparator_5 (.a(opcode), .b(7'b1100011), .eq(comparator_5_eq));  // open: gt, lt
  Comparator #(.width(3)) comparator_6 (.a(funct3), .b(3'b100), .eq(comparator_6_eq));  // open: gt, lt
  or or_1 (or_1_out, comparator_6_eq, comparator_7_eq);
  Comparator #(.width(3)) comparator_7 (.a(funct3), .b(3'b110), .eq(comparator_7_eq));  // open: gt, lt
  or or_2 (or_2_out, comparator_1_eq, comparator_2_eq);
  and and_1 (and_1_out, BrEq, comparator_3_eq, comparator_4_eq);
  and and_2 (and_2_out, BLT, comparator_5_eq, or_1_out);
  or or_3 (Select_ALU, or_2_out, and_1_out, and_2_out);
endmodule

module ImmSel (
  input  [6:0] opcode,
  output [3:0] ImmSel
);

  wire comparator_1_eq, comparator_2_eq, comparator_3_eq, comparator_4_eq, comparator_5_eq, comparator_6_eq,
       comparator_7_eq, or_2_out;
  wire [3:0] I_type, S_type, SB_type, U_type, UJ_type;

  assign ImmSel = I_type | S_type | SB_type | U_type | UJ_type;  // OR_Gate or_1, 4 bits wide
  Comparator #(.width(7)) comparator_1 (.a(opcode), .b(7'b0000011), .eq(comparator_1_eq));  // open: gt, lt
  Comparator #(.width(7)) comparator_2 (.a(opcode), .b(7'b0010011), .eq(comparator_2_eq));  // open: gt, lt
  Comparator #(.width(7)) comparator_3 (.a(opcode), .b(7'b1100111), .eq(comparator_3_eq));  // open: gt, lt
  Comparator #(.width(7)) comparator_4 (.a(opcode), .b(7'b0100011), .eq(comparator_4_eq));  // open: gt, lt
  Comparator #(.width(7)) comparator_5 (.a(opcode), .b(7'b1100011), .eq(comparator_5_eq));  // open: gt, lt
  Comparator #(.width(7)) comparator_6 (.a(opcode), .b(7'b0110111), .eq(comparator_6_eq));  // open: gt, lt
  Comparator #(.width(7)) comparator_7 (.a(opcode), .b(7'b1101111), .eq(comparator_7_eq));  // open: gt, lt
  or or_2 (or_2_out, comparator_1_eq, comparator_2_eq, comparator_3_eq);
  Multiplexer #(.width(4)) multiplexer_1 (.in0(4'b0000), .in1(4'b0001), .out(I_type), .sel(or_2_out));  // open: en
  Multiplexer #(.width(4)) multiplexer_2 (
    .in0(4'b0000), .in1(4'b0010), .out(S_type), .sel(comparator_4_eq));  // open: en
  Multiplexer #(.width(4)) multiplexer_3 (
    .in0(4'b0000), .in1(4'b0011), .out(SB_type), .sel(comparator_5_eq));  // open: en
  Multiplexer #(.width(4)) multiplexer_4 (
    .in0(4'b0000), .in1(4'b0100), .out(U_type), .sel(comparator_6_eq));  // open: en
  Multiplexer #(.width(4)) multiplexer_5 (
    .in0(4'b0000), .in1(4'b0101), .out(UJ_type), .sel(comparator_7_eq));  // open: en
endmodule

module ALUSel (
  input  [6:0] OP,
  input  [2:0] FUNCT3,
  input  [6:0] FUNCT7,
  output [3:0] out_4
);

  wire and_1_out, and_2_out, and_3_out, and_4_out, and_5_out, and_6_out, and_7_out, and_8_out, and_9_out,
       and_10_out, and_11_out, and_12_out, and_13_out, and_14_out, and_15_out, and_16_out, and_17_out,
       and_18_out, and_19_out, and_20_out, and_21_out, and_22_out, and_23_out, and_24_out, comparator_1_eq,
       comparator_2_eq, comparator_3_eq, comparator_4_eq, comparator_5_eq, comparator_6_eq, comparator_7_eq,
       comparator_8_eq, comparator_9_eq, comparator_10_eq, comparator_11_eq, comparator_12_eq,
       comparator_13_eq, comparator_14_eq, comparator_15_eq, comparator_16_eq, comparator_17_eq,
       comparator_18_eq, comparator_19_eq, comparator_20_eq, comparator_21_eq, comparator_22_eq,
       comparator_23_eq, comparator_24_eq, comparator_25_eq, comparator_26_eq, comparator_27_eq,
       comparator_28_eq, comparator_29_eq, comparator_30_eq, comparator_31_eq, comparator_32_eq,
       comparator_33_eq, comparator_34_eq, comparator_35_eq, comparator_36_eq, comparator_37_eq,
       comparator_38_eq, comparator_39_eq, comparator_40_eq, comparator_41_eq, comparator_42_eq,
       comparator_43_eq, comparator_44_eq, comparator_45_eq, comparator_46_eq, comparator_47_eq,
       comparator_48_eq, comparator_49_eq, comparator_50_eq, comparator_51_eq, comparator_52_eq,
       comparator_53_eq, comparator_54_eq, comparator_55_eq, comparator_56_eq, comparator_57_eq,
       comparator_58_eq, comparator_59_eq, comparator_60_eq, comparator_61_eq, comparator_62_eq,
       comparator_63_eq, comparator_64_eq, comparator_65_eq, comparator_66_eq, comparator_67_eq, or_2_out,
       or_3_out, or_4_out, or_5_out, or_6_out, or_7_out, or_8_out;
  wire [3:0] ADD, AND, DIV, MUL, MULH, OR, or_1_out, REM, SLL, SLT, SRL, SUB, SWGE, XOR;

  assign or_1_out = ADD | AND | OR | XOR | SRL | SLL | SLT | DIV | REM | MUL | MULH | SUB | SWGE;  // OR_Gate or_1, 4 bits wide
  Subtractor #(.width(4)) subtractor_1 (.a(or_1_out), .b(4'b0001), .out(out_4));  // open: bin, bout
  Comparator #(.width(7)) comparator_1 (.a(OP), .b(7'b0110011), .eq(comparator_1_eq));  // open: gt, lt
  Comparator #(.width(3)) comparator_2 (.a(FUNCT3), .b(3'b000), .eq(comparator_2_eq));  // open: gt, lt
  Comparator #(.width(7)) comparator_3 (.a(FUNCT7), .b({7{1'b0}}), .eq(comparator_3_eq));  // open: gt, lt
  Comparator #(.width(7)) comparator_4 (.a(OP), .b(7'b0010011), .eq(comparator_4_eq));  // open: gt, lt
  Comparator #(.width(3)) comparator_5 (.a(FUNCT3), .b(3'b000), .eq(comparator_5_eq));  // open: gt, lt
  Comparator #(.width(7)) comparator_6 (.a(OP), .b(7'b0000011), .eq(comparator_6_eq));  // open: gt, lt
  Comparator #(.width(7)) comparator_7 (.a(OP), .b(7'b0100011), .eq(comparator_7_eq));  // open: gt, lt
  Comparator #(.width(3)) comparator_8 (.a(FUNCT3), .b(3'b010), .eq(comparator_8_eq));  // open: gt, lt
  Comparator #(.width(7)) comparator_9 (.a(OP), .b(7'b1100011), .eq(comparator_9_eq));  // open: gt, lt
  Comparator #(.width(7)) comparator_10 (.a(OP), .b(7'b1101111), .eq(comparator_10_eq));  // open: gt, lt
  Comparator #(.width(7)) comparator_11 (.a(OP), .b(7'b1100111), .eq(comparator_11_eq));  // open: gt, lt
  Comparator #(.width(3)) comparator_12 (.a(FUNCT3), .b(3'b000), .eq(comparator_12_eq));  // open: gt, lt
  Comparator #(.width(7)) comparator_13 (.a(OP), .b(7'b0110011), .eq(comparator_13_eq));  // open: gt, lt
  Comparator #(.width(3)) comparator_14 (.a(FUNCT3), .b(3'b111), .eq(comparator_14_eq));  // open: gt, lt
  Comparator #(.width(7)) comparator_15 (.a(OP), .b(7'b0010011), .eq(comparator_15_eq));  // open: gt, lt
  Comparator #(.width(3)) comparator_16 (.a(FUNCT3), .b(3'b111), .eq(comparator_16_eq));  // open: gt, lt
  Comparator #(.width(7)) comparator_17 (.a(OP), .b(7'b0110011), .eq(comparator_17_eq));  // open: gt, lt
  Comparator #(.width(3)) comparator_18 (.a(FUNCT3), .b(3'b110), .eq(comparator_18_eq));  // open: gt, lt
  Comparator #(.width(7)) comparator_19 (.a(FUNCT7), .b(7'b0000001), .eq(comparator_19_eq));  // open: gt, lt
  Comparator #(.width(7)) comparator_20 (.a(OP), .b(7'b0010011), .eq(comparator_20_eq));  // open: gt, lt
  Comparator #(.width(3)) comparator_21 (.a(FUNCT3), .b(3'b110), .eq(comparator_21_eq));  // open: gt, lt
  Comparator #(.width(7)) comparator_22 (.a(OP), .b(7'b0110011), .eq(comparator_22_eq));  // open: gt, lt
  Comparator #(.width(3)) comparator_23 (.a(FUNCT3), .b(3'b100), .eq(comparator_23_eq));  // open: gt, lt
  Comparator #(.width(7)) comparator_24 (.a(FUNCT7), .b({7{1'b0}}), .eq(comparator_24_eq));  // open: gt, lt
  Comparator #(.width(7)) comparator_25 (.a(OP), .b(7'b0010011), .eq(comparator_25_eq));  // open: gt, lt
  Comparator #(.width(3)) comparator_26 (.a(FUNCT3), .b(3'b100), .eq(comparator_26_eq));  // open: gt, lt
  Comparator #(.width(7)) comparator_27 (.a(OP), .b(7'b0110011), .eq(comparator_27_eq));  // open: gt, lt
  Comparator #(.width(3)) comparator_28 (.a(FUNCT3), .b(3'b101), .eq(comparator_28_eq));  // open: gt, lt
  Comparator #(.width(7)) comparator_29 (.a(FUNCT7), .b({7{1'b0}}), .eq(comparator_29_eq));  // open: gt, lt
  Comparator #(.width(7)) comparator_30 (.a(OP), .b(7'b0010011), .eq(comparator_30_eq));  // open: gt, lt
  Comparator #(.width(3)) comparator_31 (.a(FUNCT3), .b(3'b101), .eq(comparator_31_eq));  // open: gt, lt
  Comparator #(.width(7)) comparator_32 (.a(FUNCT7), .b({7{1'b0}}), .eq(comparator_32_eq));  // open: gt, lt
  Comparator #(.width(7)) comparator_33 (.a(OP), .b(7'b0110011), .eq(comparator_33_eq));  // open: gt, lt
  Comparator #(.width(3)) comparator_34 (.a(FUNCT3), .b(3'b101), .eq(comparator_34_eq));  // open: gt, lt
  Comparator #(.width(7)) comparator_35 (.a(FUNCT7), .b({7{1'b0}}), .eq(comparator_35_eq));  // open: gt, lt
  Comparator #(.width(7)) comparator_36 (.a(OP), .b(7'b0010011), .eq(comparator_36_eq));  // open: gt, lt
  Comparator #(.width(3)) comparator_37 (.a(FUNCT3), .b(3'b101), .eq(comparator_37_eq));  // open: gt, lt
  Comparator #(.width(7)) comparator_38 (.a(FUNCT7), .b({7{1'b0}}), .eq(comparator_38_eq));  // open: gt, lt
  Comparator #(.width(7)) comparator_39 (.a(OP), .b(7'b0110011), .eq(comparator_39_eq));  // open: gt, lt
  Comparator #(.width(3)) comparator_40 (.a(FUNCT3), .b(3'b001), .eq(comparator_40_eq));  // open: gt, lt
  Comparator #(.width(7)) comparator_41 (.a(FUNCT7), .b({7{1'b0}}), .eq(comparator_41_eq));  // open: gt, lt
  Comparator #(.width(7)) comparator_42 (.a(OP), .b(7'b0010011), .eq(comparator_42_eq));  // open: gt, lt
  Comparator #(.width(3)) comparator_43 (.a(FUNCT3), .b(3'b001), .eq(comparator_43_eq));  // open: gt, lt
  Comparator #(.width(7)) comparator_44 (.a(FUNCT7), .b({7{1'b0}}), .eq(comparator_44_eq));  // open: gt, lt
  Comparator #(.width(7)) comparator_45 (.a(OP), .b(7'b0110011), .eq(comparator_45_eq));  // open: gt, lt
  Comparator #(.width(3)) comparator_46 (.a(FUNCT3), .b(3'b010), .eq(comparator_46_eq));  // open: gt, lt
  Comparator #(.width(7)) comparator_47 (.a(FUNCT7), .b({7{1'b0}}), .eq(comparator_47_eq));  // open: gt, lt
  Comparator #(.width(7)) comparator_48 (.a(OP), .b(7'b0010011), .eq(comparator_48_eq));  // open: gt, lt
  Comparator #(.width(3)) comparator_49 (.a(FUNCT3), .b(3'b010), .eq(comparator_49_eq));  // open: gt, lt
  Comparator #(.width(7)) comparator_50 (.a(OP), .b(7'b0110011), .eq(comparator_50_eq));  // open: gt, lt
  Comparator #(.width(3)) comparator_51 (.a(FUNCT3), .b(3'b100), .eq(comparator_51_eq));  // open: gt, lt
  Comparator #(.width(7)) comparator_52 (.a(FUNCT7), .b(7'b0000001), .eq(comparator_52_eq));  // open: gt, lt
  Comparator #(.width(7)) comparator_53 (.a(OP), .b(7'b0110011), .eq(comparator_53_eq));  // open: gt, lt
  Comparator #(.width(3)) comparator_54 (.a(FUNCT3), .b(3'b110), .eq(comparator_54_eq));  // open: gt, lt
  Comparator #(.width(7)) comparator_55 (.a(FUNCT7), .b(7'b0000001), .eq(comparator_55_eq));  // open: gt, lt
  Comparator #(.width(7)) comparator_56 (.a(OP), .b(7'b0110011), .eq(comparator_56_eq));  // open: gt, lt
  Comparator #(.width(3)) comparator_57 (.a(FUNCT3), .b(3'b000), .eq(comparator_57_eq));  // open: gt, lt
  Comparator #(.width(7)) comparator_58 (.a(FUNCT7), .b(7'b0000001), .eq(comparator_58_eq));  // open: gt, lt
  Comparator #(.width(7)) comparator_59 (.a(OP), .b(7'b0110011), .eq(comparator_59_eq));  // open: gt, lt
  Comparator #(.width(3)) comparator_60 (.a(FUNCT3), .b(3'b001), .eq(comparator_60_eq));  // open: gt, lt
  Comparator #(.width(7)) comparator_61 (.a(FUNCT7), .b(7'b0000001), .eq(comparator_61_eq));  // open: gt, lt
  Comparator #(.width(7)) comparator_62 (.a(OP), .b(7'b0110011), .eq(comparator_62_eq));  // open: gt, lt
  Comparator #(.width(3)) comparator_63 (.a(FUNCT3), .b(3'b000), .eq(comparator_63_eq));  // open: gt, lt
  Comparator #(.width(7)) comparator_64 (.a(FUNCT7), .b(7'b0100000), .eq(comparator_64_eq));  // open: gt, lt
  Comparator #(.width(7)) comparator_65 (.a(OP), .b(7'b0100011), .eq(comparator_65_eq));  // open: gt, lt
  Comparator #(.width(3)) comparator_66 (.a(FUNCT3), .b(3'b111), .eq(comparator_66_eq));  // open: gt, lt
  and and_1 (and_1_out, comparator_1_eq, comparator_2_eq, comparator_3_eq);
  and and_2 (and_2_out, comparator_4_eq, comparator_5_eq);
  and and_3 (and_3_out, comparator_7_eq, comparator_8_eq);
  and and_4 (and_4_out, comparator_11_eq, comparator_12_eq);
  and and_5 (and_5_out, comparator_13_eq, comparator_14_eq);
  and and_6 (and_6_out, comparator_15_eq, comparator_16_eq);
  and and_7 (and_7_out, comparator_17_eq, comparator_18_eq, comparator_19_eq);
  and and_8 (and_8_out, comparator_20_eq, comparator_21_eq);
  and and_9 (and_9_out, comparator_22_eq, comparator_23_eq, comparator_24_eq);
  and and_10 (and_10_out, comparator_25_eq, comparator_26_eq);
  and and_11 (and_11_out, comparator_27_eq, comparator_28_eq, comparator_29_eq);
  and and_12 (and_12_out, comparator_30_eq, comparator_31_eq, comparator_32_eq);
  and and_13 (and_13_out, comparator_33_eq, comparator_34_eq, comparator_35_eq);
  and and_14 (and_14_out, comparator_36_eq, comparator_38_eq);
  and and_15 (and_15_out, comparator_39_eq, comparator_40_eq, comparator_41_eq);
  and and_16 (and_16_out, comparator_42_eq, comparator_43_eq, comparator_44_eq);
  and and_17 (and_17_out, comparator_45_eq, comparator_46_eq, comparator_47_eq);
  and and_18 (and_18_out, comparator_48_eq, comparator_49_eq);
  and and_19 (and_19_out, comparator_50_eq, comparator_51_eq, comparator_52_eq);
  and and_20 (and_20_out, comparator_53_eq, comparator_54_eq, comparator_55_eq);
  and and_21 (and_21_out, comparator_56_eq, comparator_57_eq, comparator_58_eq);
  and and_22 (and_22_out, comparator_59_eq, comparator_60_eq, comparator_61_eq);
  and and_23 (and_23_out, comparator_62_eq, comparator_63_eq, comparator_64_eq);
  and and_24 (and_24_out, comparator_65_eq, comparator_66_eq);
  or or_2 (or_2_out, and_5_out, and_6_out);
  or or_3 (or_3_out, and_7_out, and_8_out);
  or or_4 (or_4_out, and_9_out, and_10_out);
  or or_5 (or_5_out, and_11_out, and_12_out);
  or or_6 (or_6_out, and_15_out, and_16_out);
  or or_7 (or_7_out, and_17_out, and_18_out);
  Multiplexer #(.width(4)) multiplexer_1 (.in0(4'b0000), .in1(4'b1001), .out(DIV), .sel(and_19_out));  // open: en
  Multiplexer #(.width(4)) multiplexer_2 (.in0(4'b0000), .in1(4'b1010), .out(REM), .sel(and_20_out));  // open: en
  Multiplexer #(.width(4)) multiplexer_3 (.in0(4'b0000), .in1(4'b1011), .out(MUL), .sel(and_21_out));  // open: en
  Multiplexer #(.width(4)) multiplexer_4 (.in0(4'b0000), .in1(4'b1100), .out(MULH), .sel(and_22_out));  // open: en
  Multiplexer #(.width(4)) multiplexer_5 (.in0(4'b0000), .in1(4'b1101), .out(SUB), .sel(and_23_out));  // open: en
  Multiplexer #(.width(4)) multiplexer_6 (.in0(4'b0000), .in1(4'b1110), .out(SWGE), .sel(and_24_out));  // open: en
  Comparator #(.width(7)) comparator_67 (.a(OP), .b(7'b0110111), .eq(comparator_67_eq));  // open: gt, lt
  Multiplexer #(.width(4)) multiplexer_7 (.in0(4'b0000), .in1(4'b0010), .out(AND), .sel(or_2_out));  // open: en
  Multiplexer #(.width(4)) multiplexer_8 (.in0(4'b0000), .in1(4'b0011), .out(OR), .sel(or_3_out));  // open: en
  Multiplexer #(.width(4)) multiplexer_9 (.in0(4'b0000), .in1(4'b0100), .out(XOR), .sel(or_4_out));  // open: en
  Multiplexer #(.width(4)) multiplexer_10 (.in0(4'b0000), .in1(4'b0101), .out(SRL), .sel(or_5_out));  // open: en
  Multiplexer #(.width(4)) multiplexer_11 (.in0(4'b0000), .in1(4'b0111), .out(SLL), .sel(or_6_out));  // open: en
  Multiplexer #(.width(4)) multiplexer_12 (.in0(4'b0000), .in1(4'b1000), .out(SLT), .sel(or_7_out));  // open: en
  Multiplexer #(.width(4)) multiplexer_13 (.in0(4'b0000), .in1(4'b0001), .out(ADD), .sel(or_8_out));  // open: en
  or or_8 (or_8_out, comparator_67_eq, and_1_out, and_2_out, comparator_6_eq, and_3_out, comparator_9_eq, comparator_10_eq, and_4_out);

  // Other names for the same wires on the sheet: f3[2:0] = FUNCT3; f7[6:0] = FUNCT7; opcode[6:0] = OP

  // Notes on the sheet:
  //   ADD / R-type
  //   ADD / I-type (not load)
  //   ADD / LOAD
  //   ADD / SW ONLY
  //   ADD / SB
  //   ADD / JAL
  //   ADD / JALR
  //   AND
  //   ANDI
  //   OR
  //   ORI
  //   XOR
  //   XORI
  //   SRL
  //   SRLI
  //   SRA??????
  //   SRAI?????
  //   SLL
  //   SLLI
  //   SLT
  //   SLTI
  //   DIV
  //   REM
  //   MUL
  //   MULH
  //   SUB
  //   SWGE
endmodule

module ABSel (
  input  [6:0] opcode,
  input  [2:0] funct3,
  output ASel,
  output BSel
);

  wire and_1_out, comparator_1_eq, comparator_2_eq, comparator_3_eq, comparator_4_eq, comparator_5_eq,
       comparator_6_eq, comparator_7_eq, comparator_8_eq, multiplexer_2_out, or_1_out, or_2_out;

  Comparator #(.width(7)) comparator_1 (.a(opcode), .b(7'b1100111), .eq(comparator_1_eq));  // open: gt, lt
  Comparator #(.width(7)) comparator_2 (.a(opcode), .b(7'b0110111), .eq(comparator_2_eq));  // open: gt, lt
  Comparator #(.width(7)) comparator_3 (.a(opcode), .b(7'b0000011), .eq(comparator_3_eq));  // open: gt, lt
  Comparator #(.width(7)) comparator_4 (.a(opcode), .b(7'b0010011), .eq(comparator_4_eq));  // open: gt, lt
  Comparator #(.width(7)) comparator_5 (.a(opcode), .b(7'b0100011), .eq(comparator_5_eq));  // open: gt, lt
  Comparator #(.width(3)) comparator_6 (.a(funct3), .b(3'b010), .eq(comparator_6_eq));  // open: gt, lt
  Comparator #(.width(7)) comparator_7 (.a(opcode), .b(7'b1100011), .eq(comparator_7_eq));  // open: gt, lt
  Comparator #(.width(7)) comparator_8 (.a(opcode), .b(7'b1101111), .eq(comparator_8_eq));  // open: gt, lt
  and and_1 (and_1_out, comparator_5_eq, comparator_6_eq);
  or or_1 (or_1_out, comparator_7_eq, comparator_8_eq);
  or or_2 (or_2_out, comparator_1_eq, comparator_2_eq, comparator_3_eq, comparator_4_eq, and_1_out);
  Multiplexer multiplexer_1 (.in0(1'b0), .in1(1'b1), .out(ASel), .sel(or_1_out));  // open: en
  Multiplexer multiplexer_2 (.in0(1'b0), .in1(1'b1), .out(multiplexer_2_out), .sel(or_2_out));  // open: en
  or or_3 (BSel, multiplexer_2_out, ASel);

  // Other names for the same wires on the sheet: A = ASel; B = BSel; f3[2:0] = funct3
endmodule

module WBSel (
  input  [6:0] OP,
  input  [2:0] FUNCT3,
  input  [6:0] FUNCT7,
  output [1:0] WBSel
);

  wire comparator_1_eq, comparator_2_eq, comparator_3_eq, comparator_4_eq, comparator_5_eq, or_1_out,
       or_2_out;
  wire [1:0] multiplexer_1_out, multiplexer_2_out;

  Comparator #(.width(7)) comparator_1 (.a(OP), .b(7'b0110011), .eq(comparator_1_eq));  // open: gt, lt
  Comparator #(.width(7)) comparator_2 (.a(OP), .b(7'b0010011), .eq(comparator_2_eq));  // open: gt, lt
  Comparator #(.width(7)) comparator_3 (.a(OP), .b(7'b0110111), .eq(comparator_3_eq));  // open: gt, lt
  Comparator #(.width(7)) comparator_4 (.a(OP), .b(7'b1101111), .eq(comparator_4_eq));  // open: gt, lt
  Comparator #(.width(7)) comparator_5 (.a(OP), .b(7'b1100111), .eq(comparator_5_eq));  // open: gt, lt
  or or_1 (or_1_out, comparator_1_eq, comparator_2_eq, comparator_3_eq);
  or or_2 (or_2_out, comparator_4_eq, comparator_5_eq);
  Multiplexer #(.width(2)) multiplexer_1 (
    .in0(2'b00), .in1(2'b01), .out(multiplexer_1_out), .sel(or_1_out));  // open: en
  Multiplexer #(.width(2)) multiplexer_2 (
    .in0(2'b00), .in1(2'b10), .out(multiplexer_2_out), .sel(or_2_out));  // open: en
  assign WBSel = multiplexer_1_out | multiplexer_2_out;  // OR_Gate or_3, 2 bits wide

  // Other names for the same wires on the sheet: f3[2:0] = FUNCT3; f7[6:0] = FUNCT7; opcode[6:0] = OP
endmodule

module Branch_Comparator (
  input  [31:0] in_1,
  input  [31:0] in_2,
  input  in_3,
  output BrEq,
  output BLT
);

  wire BLT_t, BLTU;

  Comparator #(.width(32)) comparator_1 (.a(in_1), .b(in_2), .eq(BrEq), .lt(BLT_t));  // open: gt
  Comparator #(.width(32), .mode("unsigned")) comparator_2 (.a(in_1), .b(in_2), .lt(BLTU));  // open: gt, eq
  Multiplexer multiplexer_1 (.in0(BLT_t), .in1(BLTU), .out(BLT), .sel(in_3));  // open: en

  // Other names for the same wires on the sheet: RS1[31:0] = in_1; RS2[31:0] = in_2
endmodule

module ImmGenerator (
  input  [31:0] Instruction,
  input  [3:0] ImmSel,
  output [31:0] Immediate
);

  wire comparator_1_lt, comparator_2_lt;
  wire [11:0] bit_extender_2_out, bit_extender_3_out, bit_extender_4_out, bit_extender_5_out,
       bit_extender_6_out, bit_extender_7_out, or_1_out, or_2_out, shifter_1_out, shifter_2_out,
       shifter_3_out, shifter_4_out;
  wire [19:0] bit_extender_8_out, bit_extender_9_out, bit_extender_10_out, bit_extender_11_out, or_3_out,
       shifter_5_out, shifter_6_out, shifter_7_out;
  wire [31:0] bit_extender_13_out, bit_extender_14_out, divider_1_out, divider_2_out, divider_3_out,
       divider_4_out, I_type, negator_1_out, negator_2_out, negator_3_out, negator_4_out, S_type, SB_type,
       shifter_8_out, shifter_9_out, U_type, UJ_type;

  Multiplexer #(.select(3), .width(32)) multiplexer_1 (
    .in0(Instruction), .in1(I_type), .in2(S_type), .in3(SB_type), .in4(U_type), .in5(UJ_type),
    .out(Immediate), .sel(ImmSel[2:0]));  // open: in6, in7, en
  assign I_type = {{20{Instruction[31]}}, Instruction[31:20]};  // Bit_Extender bit_extender_1
  assign bit_extender_2_out = {{5{1'b0}}, Instruction[31:25]};  // Bit_Extender bit_extender_2
  assign bit_extender_3_out = {{7{1'b0}}, Instruction[11:7]};  // Bit_Extender bit_extender_3
  assign bit_extender_4_out = {{11{1'b0}}, Instruction[31]};  // Bit_Extender bit_extender_4
  assign bit_extender_5_out = {{11{1'b0}}, Instruction[7]};  // Bit_Extender bit_extender_5
  assign bit_extender_6_out = {{6{1'b0}}, Instruction[30:25]};  // Bit_Extender bit_extender_6
  assign bit_extender_7_out = {{8{1'b0}}, Instruction[11:8]};  // Bit_Extender bit_extender_7
  assign bit_extender_8_out = {{19{1'b0}}, Instruction[31]};  // Bit_Extender bit_extender_8
  assign bit_extender_9_out = {{12{1'b0}}, Instruction[19:12]};  // Bit_Extender bit_extender_9
  assign bit_extender_10_out = {{19{1'b0}}, Instruction[20]};  // Bit_Extender bit_extender_10
  assign bit_extender_11_out = {{10{1'b0}}, Instruction[30:21]};  // Bit_Extender bit_extender_11
  Shifter #(.width(12)) shifter_1 (.in(bit_extender_2_out), .\dist (4'b0101), .out(shifter_1_out));
  Shifter #(.width(12)) shifter_2 (.in(bit_extender_4_out), .\dist (4'b1011), .out(shifter_2_out));
  Shifter #(.width(12)) shifter_3 (.in(bit_extender_5_out), .\dist (4'b1010), .out(shifter_3_out));
  Shifter #(.width(12)) shifter_4 (.in(bit_extender_6_out), .\dist (4'b0100), .out(shifter_4_out));
  assign U_type = Instruction & 32'hfffff000;  // AND_Gate and_1, 32 bits wide
  Shifter #(.width(20)) shifter_5 (.in(bit_extender_8_out), .\dist (5'b10011), .out(shifter_5_out));
  Shifter #(.width(20)) shifter_6 (.in(bit_extender_9_out), .\dist (5'b01011), .out(shifter_6_out));
  Shifter #(.width(20)) shifter_7 (.in(bit_extender_10_out), .\dist (5'b01010), .out(shifter_7_out));
  // Probe on I_type
  assign or_1_out = shifter_1_out | bit_extender_3_out;  // OR_Gate or_1, 12 bits wide
  assign or_2_out = shifter_2_out | shifter_3_out | shifter_4_out | bit_extender_7_out;  // OR_Gate or_2, 12 bits wide
  assign or_3_out = shifter_5_out | shifter_6_out | shifter_7_out | bit_extender_11_out;  // OR_Gate or_3, 20 bits wide
  assign S_type = {{20{or_1_out[11]}}, or_1_out};  // Bit_Extender bit_extender_12
  assign bit_extender_13_out = {{20{or_2_out[11]}}, or_2_out};  // Bit_Extender bit_extender_13
  // Probe on U_type
  assign bit_extender_14_out = {{12{or_3_out[19]}}, or_3_out};  // Bit_Extender bit_extender_14
  // Probe on S_type
  Shifter #(.width(32)) shifter_8 (.in(bit_extender_13_out), .\dist (5'b00001), .out(shifter_8_out));
  Shifter #(.width(32)) shifter_9 (.in(bit_extender_14_out), .\dist (5'b00001), .out(shifter_9_out));
  Negator #(.width(32)) negator_1 (.in(shifter_8_out), .out(negator_1_out));
  Comparator #(.width(32)) comparator_1 (.a(shifter_8_out), .b({32{1'b0}}), .lt(comparator_1_lt));  // open: gt, eq
  Negator #(.width(32)) negator_2 (.in(shifter_9_out), .out(negator_2_out));
  Comparator #(.width(32)) comparator_2 (.a(shifter_9_out), .b({32{1'b0}}), .lt(comparator_2_lt));  // open: gt, eq
  Divider #(.width(32)) divider_1 (.a(shifter_8_out), .b(32'h4), .out(divider_1_out));  // open: upper, rem
  Divider #(.width(32)) divider_2 (.a(negator_1_out), .b(32'h4), .out(divider_2_out));  // open: upper, rem
  Divider #(.width(32)) divider_3 (.a(shifter_9_out), .b(32'h4), .out(divider_3_out));  // open: upper, rem
  Divider #(.width(32)) divider_4 (.a(negator_2_out), .b(32'h4), .out(divider_4_out));  // open: upper, rem
  Negator #(.width(32)) negator_3 (.in(divider_2_out), .out(negator_3_out));
  Negator #(.width(32)) negator_4 (.in(divider_4_out), .out(negator_4_out));
  Multiplexer #(.width(32)) multiplexer_2 (
    .in0(divider_1_out), .in1(negator_3_out), .out(SB_type), .sel(comparator_1_lt));  // open: en
  Multiplexer #(.width(32)) multiplexer_3 (
    .in0(divider_3_out), .in1(negator_4_out), .out(UJ_type), .sel(comparator_2_lt));  // open: en
  // Probe on SB_type
  // Probe on UJ_type

  // Other names for the same wires on the sheet: ImmSel_t[2:0] = ImmSel[2:0]; R_type[31:0] = Instruction
endmodule

module SignExt (
  input  [31:0] MEM,
  input  [6:0] OP,
  input  [2:0] F3,
  output [31:0] OUT
);

  wire and_3_out, and_4_out, comparator_2_eq, comparator_3_eq, LOAD;
  wire [1:0] BYTE, HALF, or_3_out;
  wire [31:0] and_1_out, and_2_out, multiplexer_1_out, multiplexer_2_out, or_1_out, or_2_out;

  assign and_1_out = 32'hff & MEM;  // AND_Gate and_1, 32 bits wide
  assign or_1_out = 32'hffffff00 | MEM;  // OR_Gate or_1, 32 bits wide
  assign and_2_out = 32'hffff & MEM;  // AND_Gate and_2, 32 bits wide
  assign or_2_out = 32'hffff0000 | MEM;  // OR_Gate or_2, 32 bits wide
  Multiplexer #(.width(32)) multiplexer_1 (
    .in0(and_1_out), .in1(or_1_out), .out(multiplexer_1_out), .sel(MEM[7]));  // open: en
  Multiplexer #(.width(32)) multiplexer_2 (
    .in0(and_2_out), .in1(or_2_out), .out(multiplexer_2_out), .sel(MEM[15]));  // open: en
  Comparator #(.width(7)) comparator_1 (.a(OP), .b(7'b0000011), .eq(LOAD));  // open: gt, lt
  Comparator #(.width(3)) comparator_2 (.a(F3), .b(3'b000), .eq(comparator_2_eq));  // open: gt, lt
  Comparator #(.width(3)) comparator_3 (.a(F3), .b(3'b001), .eq(comparator_3_eq));  // open: gt, lt
  assign or_3_out = BYTE | HALF;  // OR_Gate or_3, 2 bits wide
  and and_3 (and_3_out, LOAD, comparator_2_eq);
  and and_4 (and_4_out, LOAD, comparator_3_eq);
  Multiplexer #(.select(2), .width(32)) multiplexer_3 (
    .in0(MEM), .in1(multiplexer_1_out), .in2(multiplexer_2_out), .out(OUT), .sel(or_3_out));  // open: in3, en
  Multiplexer #(.width(2)) multiplexer_4 (.in0(2'b00), .in1(2'b01), .out(BYTE), .sel(and_3_out));  // open: en
  Multiplexer #(.width(2)) multiplexer_5 (.in0(2'b00), .in1(2'b10), .out(HALF), .sel(and_4_out));  // open: en

  // Other names for the same wires on the sheet: FUNCT3[2:0] = F3; OPCODE[6:0] = OP
endmodule
