// Logisim project regfile.circ as structural Verilog: 6 circuits, main circuit main
module main (
  input  [4:0] Read_Register_1__rs1,
  input  [4:0] Read_Register_2__rs2,
  input  [4:0] Write_Register__rd,
  input  [31:0] Write_Data,
  input  Write_Enable,
  input  Clock,
  output [31:0] ra_Value,
  output [31:0] sp_Value,
  output [31:0] t0_Value,
  output [31:0] t1_Value,
  output [31:0] t2_Value,
  output [31:0] s0_Value,
  output [31:0] s1_Value,
  output [31:0] a0_Value,
  output [31:0] Read_Data_1,
  output [31:0] Read_Data_2
);

  wire undriven;
  wire [4:0] bit_extender_1_out, \reg ;
  wire [31:0] a1, w_x1, w_x2, w_x5, w_x6, w_x7, w_x8, w_x9, w_x10, w_x11, zero;

  Register #(.width(32)) x0 (.Q(zero), .clk(Clock), .clr(1'b1));  // open: D, en
  Register #(.width(32)) x7 (.D(w_x7), .en(undriven), .Q(t2_Value), .clk(Clock));  // open: clr
  Register #(.width(32)) x1 (.D(w_x1), .Q(ra_Value), .clk(Clock));  // open: en, clr
  Register #(.width(32)) x8 (.D(w_x8), .Q(s0_Value), .clk(Clock));  // open: en, clr
  Reg_MUX reg_mux_1 (
    .x0(zero), .x1(ra_Value), .x2(sp_Value), .invalid({32{1'b0}}), .invalid_2({32{1'b0}}), .x5(t0_Value),
    .x6(t1_Value), .x7(t2_Value), .x8(s0_Value), .x9(s1_Value), .x10(a0_Value), .x11(a1),
    .Input(Read_Register_1__rs1), .out_14(Read_Data_1));
  Reg_MUX reg_mux_2 (
    .x0(zero), .x1(ra_Value), .x2(sp_Value), .invalid({32{1'b0}}), .invalid_2({32{1'b0}}), .x5(t0_Value),
    .x6(t1_Value), .x7(t2_Value), .x8(s0_Value), .x9(s1_Value), .x10(a0_Value), .x11(a1),
    .Input(Read_Register_2__rs2), .out_14(Read_Data_2));
  Register #(.width(32)) x2 (.D(w_x2), .Q(sp_Value), .clk(Clock));  // open: en, clr
  Register #(.width(32)) x9 (.D(w_x9), .Q(s1_Value), .clk(Clock));  // open: en, clr
  Register #(.width(32)) x5 (.D(w_x5), .Q(t0_Value), .clk(Clock));  // open: en, clr
  Register #(.width(32)) x10 (.D(w_x10), .Q(a0_Value), .clk(Clock));  // open: en, clr
  Register #(.width(32)) x6 (.D(w_x6), .Q(t1_Value), .clk(Clock));  // open: en, clr
  Register #(.width(32)) x11 (.D(w_x11), .Q(a1), .clk(Clock));  // open: en, clr
  DEMUX demux_1 (
    .in_1(ra_Value), .in_2(sp_Value), .in_3(t0_Value), .in_4(t1_Value), .in_5(t2_Value), .in_6(s0_Value),
    .in_7(s1_Value), .in_8(a0_Value), .in_9(a1), .in_10(Write_Data), .in_11(\reg ), .out_12(w_x1),
    .out_13(w_x2), .out_14(w_x5), .out_15(w_x6), .out_16(w_x7), .out_17(w_x8), .out_18(w_x9), .out_19(w_x10),
    .out_20(w_x11));
  assign bit_extender_1_out = {{4{Write_Enable}}, Write_Enable};  // Bit_Extender bit_extender_1
  assign \reg  = Write_Register__rd & bit_extender_1_out;  // AND_Gate and_1, 5 bits wide

  // Other names for the same wires on the sheet: a0[31:0] = a0_Value; clk = Clock; ra[31:0] = ra_Value;
  //   read_data1[31:0] = Read_Data_1; read_data2[31:0] = Read_Data_2; read_reg1[4:0] = Read_Register_1__rs1;
  //   read_reg2[4:0] = Read_Register_2__rs2; s0[31:0] = s0_Value; s1[31:0] = s1_Value; sp[31:0] = sp_Value;
  //   t0[31:0] = t0_Value; t1[31:0] = t1_Value; t2[31:0] = t2_Value; write_en = Write_Enable;
  //   write_reg[4:0] = Write_Register__rd

  // Notes on the sheet:
  //   INPUTS to your circuit
  //   Read Circuit
  //   These are DEBUG/TEST outputs from your circuit.
  //   Registers
  //   I fucked up but it's okay
  //   Write Circuit
  //   OUTPUTS from your circuit
endmodule

module _2_1_MUX (
  input  [31:0] in_1,
  input  in_2,
  input  [31:0] in_3,
  output [31:0] out_4
);

  wire [31:0] and_1_out, and_2_out, bit_extender_1_out, not_1_out;

  assign bit_extender_1_out = {{31{in_2}}, in_2};  // Bit_Extender bit_extender_1
  assign not_1_out = ~bit_extender_1_out;  // NOT_Gate not_1, 32 bits wide
  assign and_1_out = in_1 & not_1_out;  // AND_Gate and_1, 32 bits wide
  assign and_2_out = bit_extender_1_out & in_3;  // AND_Gate and_2, 32 bits wide
  assign out_4 = and_1_out | and_2_out;  // OR_Gate or_1, 32 bits wide
endmodule

module _4_1_MUX (
  input  [31:0] in_1,
  input  [31:0] in_2,
  input  [31:0] in_3,
  input  [31:0] in_4,
  input  [1:0] in_5,
  output [31:0] out_6
);

  wire [31:0] n2_1_mux_1_out_4, n2_1_mux_2_out_4;

  _2_1_MUX u_2_1_mux_1 (.in_1(in_1), .in_2(in_5[0]), .in_3(in_2), .out_4(n2_1_mux_1_out_4));
  _2_1_MUX u_2_1_mux_2 (.in_1(in_3), .in_2(in_5[0]), .in_3(in_4), .out_4(n2_1_mux_2_out_4));
  _2_1_MUX u_2_1_mux_3 (.in_1(n2_1_mux_1_out_4), .in_2(in_5[1]), .in_3(n2_1_mux_2_out_4), .out_4(out_6));

  // Other names for the same wires on the sheet: s0 = in_5[0]; s1 = in_5[1]
endmodule

module Reg_MUX (
  input  [31:0] x0,
  input  [31:0] x1,
  input  [31:0] x2,
  input  [31:0] invalid,
  input  [31:0] invalid_2,
  input  [31:0] x5,
  input  [31:0] x6,
  input  [31:0] x7,
  input  [31:0] x8,
  input  [31:0] x9,
  input  [31:0] x10,
  input  [31:0] x11,
  input  [4:0] Input,
  output [31:0] out_14
);

  wire [31:0] n4_1_mux_1_out_6, n4_1_mux_2_out_6, n4_1_mux_3_out_6;

  _4_1_MUX u_4_1_mux_1 (.in_1(x0), .in_2(x1), .in_3(x2), .in_4(invalid), .in_5(Input[1:0]), .out_6(n4_1_mux_1_out_6));
  _4_1_MUX u_4_1_mux_2 (.in_1(invalid_2), .in_2(x5), .in_3(x6), .in_4(x7), .in_5(Input[1:0]), .out_6(n4_1_mux_2_out_6));
  _4_1_MUX u_4_1_mux_3 (.in_1(x8), .in_2(x9), .in_3(x10), .in_4(x11), .in_5(Input[1:0]), .out_6(n4_1_mux_3_out_6));
  _4_1_MUX u_4_1_mux_4 (
    .in_1(n4_1_mux_1_out_6), .in_2(n4_1_mux_2_out_6), .in_3(n4_1_mux_3_out_6), .in_4({32{1'b0}}),
    .in_5(Input[3:2]), .out_6(out_14));

  // Other names for the same wires on the sheet: bot2[1:0] = Input[1:0]; top2[1:0] = Input[3:2]
endmodule

module Choose_IN (
  input  [31:0] in_1,
  input  [31:0] in_2,
  input  [4:0] in_3,
  input  [4:0] in_4,
  output [31:0] out_5
);

  wire comparator_1_eq, match;

  _2_1_MUX u_2_1_mux_1 (.in_1(in_1), .in_2(match), .in_3(in_2), .out_4(out_5));
  Comparator #(.width(5), .mode("unsigned")) comparator_1 (.a(in_3), .b(in_4), .eq(comparator_1_eq));  // open: gt, lt
  not not_1 (match, comparator_1_eq);
endmodule

module DEMUX (
  input  [31:0] in_1,
  input  [31:0] in_2,
  input  [31:0] in_3,
  input  [31:0] in_4,
  input  [31:0] in_5,
  input  [31:0] in_6,
  input  [31:0] in_7,
  input  [31:0] in_8,
  input  [31:0] in_9,
  input  [31:0] in_10,
  input  [4:0] in_11,
  output [31:0] out_12,
  output [31:0] out_13,
  output [31:0] out_14,
  output [31:0] out_15,
  output [31:0] out_16,
  output [31:0] out_17,
  output [31:0] out_18,
  output [31:0] out_19,
  output [31:0] out_20
);

  Choose_IN choose_in_1 (.in_1(in_10), .in_2(in_1), .in_3(5'b00001), .in_4(in_11), .out_5(out_12));
  Choose_IN choose_in_2 (.in_1(in_10), .in_2(in_2), .in_3(5'b00010), .in_4(in_11), .out_5(out_13));
  Choose_IN choose_in_3 (.in_1(in_10), .in_2(in_3), .in_3(5'b00101), .in_4(in_11), .out_5(out_14));
  Choose_IN choose_in_4 (.in_1(in_10), .in_2(in_4), .in_3(5'b00110), .in_4(in_11), .out_5(out_15));
  Choose_IN choose_in_5 (.in_1(in_10), .in_2(in_5), .in_3(5'b00111), .in_4(in_11), .out_5(out_16));
  Choose_IN choose_in_6 (.in_1(in_10), .in_2(in_6), .in_3(5'b01000), .in_4(in_11), .out_5(out_17));
  Choose_IN choose_in_7 (.in_1(in_10), .in_2(in_7), .in_3(5'b01001), .in_4(in_11), .out_5(out_18));
  Choose_IN choose_in_8 (.in_1(in_10), .in_2(in_8), .in_3(5'b01010), .in_4(in_11), .out_5(out_19));
  Choose_IN choose_in_9 (.in_1(in_10), .in_2(in_9), .in_3(5'b01011), .in_4(in_11), .out_5(out_20));

  // Other names for the same wires on the sheet: _1[31:0] = in_1; _2[31:0] = in_2; _5[31:0] = in_3; _6[31:0] = in_4;
  //   _7[31:0] = in_5; _8[31:0] = in_6; _9[31:0] = in_7; _10[31:0] = in_8; _11[31:0] = in_9; to_write[4:0] = in_11;
  //   write_reg[31:0] = in_10
endmodule
