// Logisim project alu.circ as structural Verilog: 6 circuits, main circuit main
module main (
  input  [31:0] X,
  input  [31:0] Y,
  input  [3:0] Switch,
  output Equal,
  output [31:0] Result
);

  wire comparator_1_lt;
  wire [31:0] _01_out, _02_out, _03_out, adder_1_out, bit_extender_1_out, divider_1_out, divider_1_rem,
       multiplier_1_cout, multiplier_1_out, shifter_1_out, shifter_2_out, shifter_3_out, subtractor_1_out;

  Adder #(.width(32)) adder_1 (.a(X), .b(Y), .out(adder_1_out));  // open: cin, cout
  assign _01_out = X & Y;  // AND_Gate _01, 32 bits wide
  assign _02_out = X | Y;  // OR_Gate _02, 32 bits wide
  assign _03_out = X ^ Y;  // XOR_Gate _03, 32 bits wide
  Shifter #(.width(32), .shift("lr")) shifter_1 (.in(X), .\dist (Y[4:0]), .out(shifter_1_out));
  Shifter #(.width(32), .shift("ar")) shifter_2 (.in(X), .\dist (Y[4:0]), .out(shifter_2_out));
  Shifter #(.width(32)) shifter_3 (.in(X), .\dist (Y[4:0]), .out(shifter_3_out));
  Comparator #(.width(32)) comparator_1 (.a(X), .b(Y), .eq(Equal), .lt(comparator_1_lt));  // open: gt
  Divider #(.width(32)) divider_1 (.a(X), .b(Y), .out(divider_1_out), .rem(divider_1_rem));  // open: upper
  Multiplier #(.width(32)) multiplier_1 (.a(X), .b(Y), .out(multiplier_1_out), .cout(multiplier_1_cout));  // open: cin
  Subtractor #(.width(32)) subtractor_1 (.a(X), .b(Y), .out(subtractor_1_out));  // open: bin, bout
  assign bit_extender_1_out = {{31{1'b0}}, comparator_1_lt};  // Bit_Extender bit_extender_1
  OPMUX opmux_1 (
    .in_1(adder_1_out), .in_2(_01_out), .in_3(_02_out), .in_4(_03_out), .in_5(shifter_1_out),
    .in_6(shifter_2_out), .in_7(shifter_3_out), .in_8(bit_extender_1_out), .in_9(divider_1_out),
    .in_10(divider_1_rem), .in_11(multiplier_1_out), .in_13(multiplier_1_cout), .in_14(subtractor_1_out),
    .in_12(Switch), .out_15(Result));

  // Other names for the same wires on the sheet: S[3:0] = Switch

  // Notes on the sheet:
  //   INPUTS to your circuit
  //   DON'T CHANGE THE LOCATIONS OF THE INPUTS AND OUTPUTS!
  //   00
  //   04
  //   05
  //   06
  //   07
  //   08
  //   09
  //   10
  //   11
  //   12
  //   OUTPUTS from your circuit
endmodule

module ADD_SUB (
  input  in_1,
  input  [31:0] in_2,
  input  [31:0] in_3,
  output [31:0] out_4,
  output out_5
);

  wire n1_bit_adder_1_out_5, n1_bit_adder_2_out_5, n1_bit_adder_3_out_5, n1_bit_adder_4_out_5,
       n1_bit_adder_5_out_5, n1_bit_adder_6_out_5, n1_bit_adder_7_out_5, n1_bit_adder_8_out_5,
       n1_bit_adder_9_out_5, n1_bit_adder_10_out_5, n1_bit_adder_11_out_5, n1_bit_adder_12_out_5,
       n1_bit_adder_13_out_5, n1_bit_adder_14_out_5, n1_bit_adder_15_out_5, n1_bit_adder_16_out_5,
       n1_bit_adder_17_out_5, n1_bit_adder_18_out_5, n1_bit_adder_19_out_5, n1_bit_adder_20_out_5,
       n1_bit_adder_21_out_5, n1_bit_adder_22_out_5, n1_bit_adder_23_out_5, n1_bit_adder_24_out_5,
       n1_bit_adder_25_out_5, n1_bit_adder_26_out_5, n1_bit_adder_27_out_5, n1_bit_adder_28_out_5,
       n1_bit_adder_29_out_5, n1_bit_adder_30_out_5, n1_bit_adder_31_out_5, n1_bit_adder_32_out_5, xor_1_out,
       xor_2_out, xor_3_out, xor_4_out, xor_5_out, xor_6_out, xor_7_out, xor_8_out, xor_9_out, xor_10_out,
       xor_11_out, xor_12_out, xor_13_out, xor_14_out, xor_15_out, xor_16_out, xor_17_out, xor_18_out,
       xor_19_out, xor_20_out, xor_21_out, xor_22_out, xor_23_out, xor_24_out, xor_25_out, xor_26_out,
       xor_27_out, xor_28_out, xor_29_out, xor_30_out, xor_31_out, xor_32_out;

  xor xor_1 (xor_1_out, in_1, in_3[0]);
  xor xor_2 (xor_2_out, in_1, in_3[1]);
  xor xor_3 (xor_3_out, in_1, in_3[2]);
  xor xor_4 (xor_4_out, in_1, in_3[3]);
  xor xor_5 (xor_5_out, in_1, in_3[4]);
  xor xor_6 (xor_6_out, in_1, in_3[5]);
  xor xor_7 (xor_7_out, in_1, in_3[6]);
  xor xor_8 (xor_8_out, in_1, in_3[7]);
  xor xor_9 (xor_9_out, in_1, in_3[8]);
  xor xor_10 (xor_10_out, in_1, in_3[9]);
  xor xor_11 (xor_11_out, in_1, in_3[10]);
  xor xor_12 (xor_12_out, in_1, in_3[11]);
  xor xor_13 (xor_13_out, in_1, in_3[12]);
  xor xor_14 (xor_14_out, in_1, in_3[13]);
  xor xor_15 (xor_15_out, in_1, in_3[14]);
  xor xor_16 (xor_16_out, in_1, in_3[15]);
  xor xor_17 (xor_17_out, in_1, in_3[16]);
  xor xor_18 (xor_18_out, in_1, in_3[17]);
  xor xor_19 (xor_19_out, in_1, in_3[18]);
  xor xor_20 (xor_20_out, in_1, in_3[19]);
  xor xor_21 (xor_21_out, in_1, in_3[20]);
  xor xor_22 (xor_22_out, in_1, in_3[21]);
  xor xor_23 (xor_23_out, in_1, in_3[22]);
  xor xor_24 (xor_24_out, in_1, in_3[23]);
  xor xor_25 (xor_25_out, in_1, in_3[24]);
  xor xor_26 (xor_26_out, in_1, in_3[25]);
  xor xor_27 (xor_27_out, in_1, in_3[26]);
  xor xor_28 (xor_28_out, in_1, in_3[27]);
  xor xor_29 (xor_29_out, in_1, in_3[28]);
  xor xor_30 (xor_30_out, in_1, in_3[29]);
  xor xor_31 (xor_31_out, in_1, in_3[30]);
  xor xor_32 (xor_32_out, in_1, in_3[31]);
  _1_bit_ADDER u_1_bit_adder_1 (
    .in_2(in_2[0]), .in_3(xor_1_out), .in_1(in_1), .out_5(n1_bit_adder_1_out_5), .out_4(out_4[0]));
  _1_bit_ADDER u_1_bit_adder_2 (
    .in_2(in_2[1]), .in_3(xor_2_out), .in_1(n1_bit_adder_1_out_5), .out_5(n1_bit_adder_2_out_5),
    .out_4(out_4[1]));
  _1_bit_ADDER u_1_bit_adder_3 (
    .in_2(in_2[2]), .in_3(xor_3_out), .in_1(n1_bit_adder_2_out_5), .out_5(n1_bit_adder_3_out_5),
    .out_4(out_4[2]));
  _1_bit_ADDER u_1_bit_adder_4 (
    .in_2(in_2[3]), .in_3(xor_4_out), .in_1(n1_bit_adder_3_out_5), .out_5(n1_bit_adder_4_out_5),
    .out_4(out_4[3]));
  _1_bit_ADDER u_1_bit_adder_5 (
    .in_2(in_2[4]), .in_3(xor_5_out), .in_1(n1_bit_adder_4_out_5), .out_5(n1_bit_adder_5_out_5),
    .out_4(out_4[4]));
  _1_bit_ADDER u_1_bit_adder_6 (
    .in_2(in_2[5]), .in_3(xor_6_out), .in_1(n1_bit_adder_5_out_5), .out_5(n1_bit_adder_6_out_5),
    .out_4(out_4[5]));
  _1_bit_ADDER u_1_bit_adder_7 (
    .in_2(in_2[6]), .in_3(xor_7_out), .in_1(n1_bit_adder_6_out_5), .out_5(n1_bit_adder_7_out_5),
    .out_4(out_4[6]));
  _1_bit_ADDER u_1_bit_adder_8 (
    .in_2(in_2[7]), .in_3(xor_8_out), .in_1(n1_bit_adder_7_out_5), .out_5(n1_bit_adder_8_out_5),
    .out_4(out_4[7]));
  _1_bit_ADDER u_1_bit_adder_9 (
    .in_2(in_2[8]), .in_3(xor_9_out), .in_1(n1_bit_adder_8_out_5), .out_5(n1_bit_adder_9_out_5),
    .out_4(out_4[8]));
  _1_bit_ADDER u_1_bit_adder_10 (
    .in_2(in_2[9]), .in_3(xor_10_out), .in_1(n1_bit_adder_9_out_5), .out_5(n1_bit_adder_10_out_5),
    .out_4(out_4[9]));
  _1_bit_ADDER u_1_bit_adder_11 (
    .in_2(in_2[10]), .in_3(xor_11_out), .in_1(n1_bit_adder_10_out_5), .out_5(n1_bit_adder_11_out_5),
    .out_4(out_4[10]));
  _1_bit_ADDER u_1_bit_adder_12 (
    .in_2(in_2[11]), .in_3(xor_12_out), .in_1(n1_bit_adder_11_out_5), .out_5(n1_bit_adder_12_out_5),
    .out_4(out_4[11]));
  _1_bit_ADDER u_1_bit_adder_13 (
    .in_2(in_2[12]), .in_3(xor_13_out), .in_1(n1_bit_adder_12_out_5), .out_5(n1_bit_adder_13_out_5),
    .out_4(out_4[12]));
  _1_bit_ADDER u_1_bit_adder_14 (
    .in_2(in_2[13]), .in_3(xor_14_out), .in_1(n1_bit_adder_13_out_5), .out_5(n1_bit_adder_14_out_5),
    .out_4(out_4[13]));
  _1_bit_ADDER u_1_bit_adder_15 (
    .in_2(in_2[14]), .in_3(xor_15_out), .in_1(n1_bit_adder_14_out_5), .out_5(n1_bit_adder_15_out_5),
    .out_4(out_4[14]));
  _1_bit_ADDER u_1_bit_adder_16 (
    .in_2(in_2[15]), .in_3(xor_16_out), .in_1(n1_bit_adder_15_out_5), .out_5(n1_bit_adder_16_out_5),
    .out_4(out_4[15]));
  _1_bit_ADDER u_1_bit_adder_17 (
    .in_2(in_2[16]), .in_3(xor_17_out), .in_1(n1_bit_adder_16_out_5), .out_5(n1_bit_adder_17_out_5),
    .out_4(out_4[16]));
  _1_bit_ADDER u_1_bit_adder_18 (
    .in_2(in_2[17]), .in_3(xor_18_out), .in_1(n1_bit_adder_17_out_5), .out_5(n1_bit_adder_18_out_5),
    .out_4(out_4[17]));
  _1_bit_ADDER u_1_bit_adder_19 (
    .in_2(in_2[18]), .in_3(xor_19_out), .in_1(n1_bit_adder_18_out_5), .out_5(n1_bit_adder_19_out_5),
    .out_4(out_4[18]));
  _1_bit_ADDER u_1_bit_adder_20 (
    .in_2(in_2[19]), .in_3(xor_20_out), .in_1(n1_bit_adder_19_out_5), .out_5(n1_bit_adder_20_out_5),
    .out_4(out_4[19]));
  _1_bit_ADDER u_1_bit_adder_21 (
    .in_2(in_2[20]), .in_3(xor_21_out), .in_1(n1_bit_adder_20_out_5), .out_5(n1_bit_adder_21_out_5),
    .out_4(out_4[20]));
  _1_bit_ADDER u_1_bit_adder_22 (
    .in_2(in_2[21]), .in_3(xor_22_out), .in_1(n1_bit_adder_21_out_5), .out_5(n1_bit_adder_22_out_5),
    .out_4(out_4[21]));
  _1_bit_ADDER u_1_bit_adder_23 (
    .in_2(in_2[22]), .in_3(xor_23_out), .in_1(n1_bit_adder_22_out_5), .out_5(n1_bit_adder_23_out_5),
    .out_4(out_4[22]));
  _1_bit_ADDER u_1_bit_adder_24 (
    .in_2(in_2[23]), .in_3(xor_24_out), .in_1(n1_bit_adder_23_out_5), .out_5(n1_bit_adder_24_out_5),
    .out_4(out_4[23]));
  _1_bit_ADDER u_1_bit_adder_25 (
    .in_2(in_2[24]), .in_3(xor_25_out), .in_1(n1_bit_adder_24_out_5), .out_5(n1_bit_adder_25_out_5),
    .out_4(out_4[24]));
  _1_bit_ADDER u_1_bit_adder_26 (
    .in_2(in_2[25]), .in_3(xor_26_out), .in_1(n1_bit_adder_25_out_5), .out_5(n1_bit_adder_26_out_5),
    .out_4(out_4[25]));
  _1_bit_ADDER u_1_bit_adder_27 (
    .in_2(in_2[26]), .in_3(xor_27_out), .in_1(n1_bit_adder_26_out_5), .out_5(n1_bit_adder_27_out_5),
    .out_4(out_4[26]));
  _1_bit_ADDER u_1_bit_adder_28 (
    .in_2(in_2[27]), .in_3(xor_28_out), .in_1(n1_bit_adder_27_out_5), .out_5(n1_bit_adder_28_out_5),
    .out_4(out_4[27]));
  _1_bit_ADDER u_1_bit_adder_29 (
    .in_2(in_2[28]), .in_3(xor_29_out), .in_1(n1_bit_adder_28_out_5), .out_5(n1_bit_adder_29_out_5),
    .out_4(out_4[28]));
  _1_bit_ADDER u_1_bit_adder_30 (
    .in_2(in_2[29]), .in_3(xor_30_out), .in_1(n1_bit_adder_29_out_5), .out_5(n1_bit_adder_30_out_5),
    .out_4(out_4[29]));
  _1_bit_ADDER u_1_bit_adder_31 (
    .in_2(in_2[30]), .in_3(xor_31_out), .in_1(n1_bit_adder_30_out_5), .out_5(n1_bit_adder_31_out_5),
    .out_4(out_4[30]));
  _1_bit_ADDER u_1_bit_adder_32 (
    .in_2(in_2[31]), .in_3(xor_32_out), .in_1(n1_bit_adder_31_out_5), .out_5(n1_bit_adder_32_out_5),
    .out_4(out_4[31]));
  xor xor_33 (out_5, n1_bit_adder_30_out_5, n1_bit_adder_32_out_5);

  // Other names for the same wires on the sheet: X00 = in_2[0]; X01 = in_2[1]; X02 = in_2[2]; X03 = in_2[3];
  //   X04 = in_2[4]; X05 = in_2[5]; X06 = in_2[6]; X07 = in_2[7]; X08 = in_2[8]; X09 = in_2[9]; X10 = in_2[10];
  //   X11 = in_2[11]; X12 = in_2[12]; X13 = in_2[13]; X14 = in_2[14]; X15 = in_2[15]; X16 = in_2[16]; X17 = in_2[17];
  //   X18 = in_2[18]; X19 = in_2[19]; X20 = in_2[20]; X21 = in_2[21]; X22 = in_2[22]; X23 = in_2[23]; X24 = in_2[24];
  //   X25 = in_2[25]; X26 = in_2[26]; X27 = in_2[27]; X28 = in_2[28]; X29 = in_2[29]; X30 = in_2[30]; X31 = in_2[31];
  //   Y00 = in_3[0]; Y01 = in_3[1]; Y02 = in_3[2]; Y03 = in_3[3]; Y04 = in_3[4]; Y05 = in_3[5]; Y06 = in_3[6];
  //   Y07 = in_3[7]; Y08 = in_3[8]; Y09 = in_3[9]; Y10 = in_3[10]; Y11 = in_3[11]; Y12 = in_3[12]; Y13 = in_3[13];
  //   Y14 = in_3[14]; Y15 = in_3[15]; Y16 = in_3[16]; Y17 = in_3[17]; Y18 = in_3[18]; Y19 = in_3[19]; Y20 = in_3[20];
  //   Y21 = in_3[21]; Y22 = in_3[22]; Y23 = in_3[23]; Y24 = in_3[24]; Y25 = in_3[25]; Y26 = in_3[26]; Y27 = in_3[27];
  //   Y28 = in_3[28]; Y29 = in_3[29]; Y30 = in_3[30]; Y31 = in_3[31]
endmodule

module _1_bit_ADDER (
  input  in_1,
  input  in_2,
  input  in_3,
  output out_4,
  output out_5
);

  wire and_1_out, and_2_out, and_3_out;

  xor xor_1 (out_4, in_2, in_3, in_1);
  and and_1 (and_1_out, in_2, in_3);
  and and_2 (and_2_out, in_3, in_1);
  and and_3 (and_3_out, in_1, in_2);
  or or_1 (out_5, and_1_out, and_2_out, and_3_out);

  // Other names for the same wires on the sheet: a = in_2; b = in_3; c = in_1; c_1 = out_5; s = out_4
endmodule

module OPMUX (
  input  [31:0] in_1,
  input  [31:0] in_2,
  input  [31:0] in_3,
  input  [31:0] in_4,
  input  [31:0] in_5,
  input  [31:0] in_6,
  input  [31:0] in_7,
  input  [31:0] in_8,
  input  [31:0] in_9,
  input  [31:0] in_10,
  input  [31:0] in_11,
  input  [3:0] in_12,
  input  [31:0] in_13,
  input  [31:0] in_14,
  output [31:0] out_15
);

  wire [31:0] n4_1_mux_1_out_6, n4_1_mux_2_out_6, n4_1_mux_3_out_6;

  _4_1_MUX u_4_1_mux_1 (
    .in_1(in_1), .in_2(in_2), .in_3(in_3), .in_4(in_4), .in_5(in_12[1:0]), .out_6(n4_1_mux_1_out_6));
  _4_1_MUX u_4_1_mux_2 (
    .in_1(in_5), .in_2(in_6), .in_3(in_7), .in_4(in_8), .in_5(in_12[1:0]), .out_6(n4_1_mux_2_out_6));
  _4_1_MUX u_4_1_mux_3 (
    .in_1(in_9), .in_2(in_10), .in_3(in_11), .in_4(in_13), .in_5(in_12[1:0]), .out_6(n4_1_mux_3_out_6));
  _4_1_MUX u_4_1_mux_4 (
    .in_1(n4_1_mux_1_out_6), .in_2(n4_1_mux_2_out_6), .in_3(n4_1_mux_3_out_6), .in_4(in_14),
    .in_5(in_12[3:2]), .out_6(out_15));

  // Other names for the same wires on the sheet: ADD[31:0] = in_1; AND[31:0] = in_2; DIV[31:0] = in_9;
  //   bot2[1:0] = in_12[1:0]; top2[1:0] = in_12[3:2]; MUH[31:0] = in_13; MUL[31:0] = in_11; OR[31:0] = in_3;
  //   REM[31:0] = in_10; SLL[31:0] = in_7; SLT[31:0] = in_8; SRA[31:0] = in_6; SRL[31:0] = in_5; SUB[31:0] = in_14;
  //   XOR[31:0] = in_4
endmodule

module _2_1_MUX (
  input  [31:0] in_1,
  input  in_2,
  input  [31:0] in_3,
  output [31:0] out_4
);

  wire [31:0] and_1_out, and_2_out, bit_extender_1_out, not_1_out;

  assign bit_extender_1_out = {{31{in_2}}, in_2};  // Bit_Extender bit_extender_1
  assign not_1_out = ~bit_extender_1_out;  // NOT_Gate not_1, 32 bits wide
  assign and_1_out = in_1 & not_1_out;  // AND_Gate and_1, 32 bits wide
  assign and_2_out = bit_extender_1_out & in_3;  // AND_Gate and_2, 32 bits wide
  assign out_4 = and_1_out | and_2_out;  // OR_Gate or_1, 32 bits wide
endmodule

module _4_1_MUX (
  input  [31:0] in_1,
  input  [31:0] in_2,
  input  [31:0] in_3,
  input  [31:0] in_4,
  input  [1:0] in_5,
  output [31:0] out_6
);

  wire [31:0] n2_1_mux_1_out_4, n2_1_mux_2_out_4;

  _2_1_MUX u_2_1_mux_1 (.in_1(in_1), .in_2(in_5[0]), .in_3(in_2), .out_4(n2_1_mux_1_out_4));
  _2_1_MUX u_2_1_mux_2 (.in_1(in_3), .in_2(in_5[0]), .in_3(in_4), .out_4(n2_1_mux_2_out_4));
  _2_1_MUX u_2_1_mux_3 (.in_1(n2_1_mux_1_out_4), .in_2(in_5[1]), .in_3(n2_1_mux_2_out_4), .out_4(out_6));

  // Other names for the same wires on the sheet: s0 = in_5[0]; s1 = in_5[1]
endmodule
